// Logisim project pipelined.circ as structural Verilog
module main (
);

  wire button_1_out, clock_1_out, not_1_out, undriven_2, undriven_4, undriven_5, undriven_8, undriven_9,
       undriven_10, undriven_11, undriven_12;
  wire [7:0] adder_1_out, if_id_latch_1_pc_plus1_out, PC_q, RegistertoAddress_address, undriven;
  wire [15:0] if_id_latch_1_instruction_out, ram_1_data, register_1_q, rom_1_data, undriven_3, undriven_6,
       undriven_7, wb_section_1_writedata;

  Clock clock_1 (.out(clock_1_out));
  Register PC (.D(undriven), .en(not_1_out), .Q(PC_q), .clk(clock_1_out), .clr(button_1_out));
  not not_1 (not_1_out, undriven_2);
  Button button_1 (.out(button_1_out));
  Decoder Decoder ();  // open: Opcode, Subop, Zero, Less, ShiftSrc, ShifterToReg, RegWrite, ALUOp, IMMtoALU, RegtoPC, IMMtoPC, ZerosToALU, MemWrite, MemtoReg, Halt, LED, WriteLED, MemRead, PCtoReg
  Adder adder_1 (.a(PC_q), .b(8'h1), .out(adder_1_out));  // open: cin, cout
  ROM #(.dataWidth(16)) rom_1 (.addr(PC_q), .data(rom_1_data), .sel(1'b1));
  IF_ID_LATCH if_id_latch_1 (
    .Instruction_IN(rom_1_data), .PC_PLUS1_IN(adder_1_out), .Clock(clock_1_out),
    .Instruction_OUT(if_id_latch_1_instruction_out), .PC_PLUS1_OUT(if_id_latch_1_pc_plus1_out));
  ID_SECTION id_section_1 (
    .Instruction(if_id_latch_1_instruction_out), .Clock(clock_1_out), .WriteData(wb_section_1_writedata),
    .PC_PLUS1(if_id_latch_1_pc_plus1_out));  // open: WriteReg, WriteEnable, Subop, PC_PLUS1_2, ReadData1, ReadData2, IMM_ext
  ID_SECTION id_section_2 ();  // open: Instruction, Clock, WriteReg, WriteData, WriteEnable, PC_PLUS1, Subop, PC_PLUS1_2, ReadData1, ReadData2, IMM_ext
  ID_EX_LATCH id_ex_latch_1 ();  // open: in_1, in_2, in_3, in_4, in_5, in_6, in_7, in_8, in_9
  EX_SECTION ex_section_1 ();  // open: ALUOp, Subop, ReadData1, EQZ_EQP, ShiftSrc, Shamt, ReadData2, IMM_ext, IMMtoALU, ZeroestoALU, Branch, Branch_2, ALU_OUT
  MEM_SECTION mem_section_1 ();  // open: ReadData2, in_2, MemWrite, MemRead, Clock, Data_OUT
  WB_SECTION wb_section_1 (.WriteData(wb_section_1_writedata));  // open: Data_OUT, MemtoReg, ALU_OUT, PCtoReg, ShifterToReg, Shifter_OUT, ReadData1, WriteLED, PC_PLUS1, Clock, LEDDIsplayOUT
  ALUtoPC RegistertoAddress (.ALUOut(undriven_6), .Address(RegistertoAddress_address));
  Hex_Digit_Display hex_digit_display_1 (.value(register_1_q[15:12]));  // open: dp
  Register #(.width(16)) register_1 (.D(undriven_3), .en(undriven_9), .Q(register_1_q), .clk(undriven_4));  // open: clr
  LED Halt (.in(undriven_5));
  Hex_Digit_Display hex_digit_display_2 (.value(register_1_q[11:8]));  // open: dp
  Hex_Digit_Display hex_digit_display_3 (.value(register_1_q[7:4]));  // open: dp
  Hex_Digit_Display hex_digit_display_4 (.value(register_1_q[3:0]));  // open: dp
  RAM #(.dataWidth(16), .bus("separate")) ram_1 (
    .addr(RegistertoAddress_address), .din(undriven_7), .data(ram_1_data), .str(undriven_8),
    .sel(undriven_10), .clk(undriven_11), .ld(undriven_12));  // open: clr

  // Notes on the sheet:
  //   contents of rom_1 (hex, n*v repeats v):
  //   1 1104 241 1303 40 f000 241 1300 481 1503 281 6c1 1705 2c1 f200 901 1900 18ff f800 b41 1bf0 1b0f
  //   fa00 d81 1d19 fc1 1f20 3dc0 fc00 1 11e0 241 1378 3041 f000 481 150d 6c1 1708 44c0 f400 901 1910 b41
  //   1b04 4941 f800 d81 1d02 5c02 fc00 fc1 1f10 5e03 fe00 1 1140 61c1 63c0 f200 481 15ff 6c1 1701 845b
  //   865b 901 1900 985f b41 1b00 d81 1d00 1ce9 aa63 ac63 fc1 1f00 1 1119 be67 b067 e054 7000 c259 6c1
  //   170a f600 7000 d200 7000 fc1 1f01 fe00 7000 fc1 1f02 fe00 7000 fc1 1f03 fe00 7000 fc1 1f04 fe00 7000
  //   IF/ID
  //   ID
  //   IF/EX
  //   EX
  //   MEM
  //   WB
endmodule

module InstructionSplitter (
  input  [15:0] Instruction,
  output [3:0] Opcode,
  output [2:0] ReadRegister1,
  output [2:0] ReadRegister2,
  output [2:0] WriteRegister,
  output [3:0] ShiftAmount,
  output SubOp,
  output Unsigned,
  output [7:0] Immediate
);


  assign Immediate = Instruction[7:0];
  assign Opcode = Instruction[15:12];
  assign ReadRegister1 = Instruction[11:9];
  assign ReadRegister2 = Instruction[8:6];
  assign ShiftAmount = Instruction[4:1];
  assign SubOp = Instruction[0];
  assign Unsigned = Instruction[8];
  assign WriteRegister = Instruction[11:9];
endmodule

module SignExtend (
  input  Unsigned,
  input  [7:0] Immediate,
  output [15:0] SignExtendedImm
);

  wire [15:0] bit_extender_1_out, bit_extender_2_out;

  assign bit_extender_1_out = {{8{Immediate[7]}}, Immediate};  // Bit_Extender bit_extender_1
  assign bit_extender_2_out = {{8{1'b0}}, Immediate};  // Bit_Extender bit_extender_2
  Multiplexer #(.width(16), .disabled(0), .enable("false")) multiplexer_1 (
    .in0(bit_extender_1_out), .in1(bit_extender_2_out), .out(SignExtendedImm), .sel(Unsigned));
endmodule

module ALUtoPC (
  input  [15:0] ALUOut,
  output [7:0] Address
);


  assign Address = ALUOut[7:0];
endmodule

module Shifter (
  input  Subop,
  input  [15:0] Data,
  input  [15:0] ShamtReg,
  input  ShiftSrc,
  input  [3:0] Shamt,
  output [15:0] ShiftOut
);

  wire [3:0] multiplexer_1_out;
  wire [15:0] shifter_1_out, shifter_2_out;

  Multiplexer #(.width(4), .disabled(0), .enable("false")) multiplexer_1 (
    .in0(ShamtReg[3:0]), .in1(Shamt), .out(multiplexer_1_out), .sel(ShiftSrc));
  Shifter_part #(.width(16)) shifter_1 (.in(Data), .\dist (multiplexer_1_out), .out(shifter_1_out));
  Shifter_part #(.width(16), .shift("lr")) shifter_2 (.in(Data), .\dist (multiplexer_1_out), .out(shifter_2_out));
  Multiplexer #(.width(16), .disabled(0), .enable("false")) multiplexer_2 (
    .in0(shifter_1_out), .in1(shifter_2_out), .out(ShiftOut), .sel(Subop));
endmodule

module RegisterFile (
  input  [2:0] ReadRegister1,
  input  [2:0] ReadRegister2,
  input  [2:0] WriteRegister,
  input  [15:0] WriteData,
  input  WriteEnable,
  input  Clock,
  output [15:0] ReadData1,
  output [15:0] ReadData2
);

  wire decoder_1_out0, decoder_1_out1, decoder_1_out2, decoder_1_out3, decoder_1_out4, decoder_1_out5,
       decoder_1_out6, decoder_1_out7;
  wire [15:0] register_1_q, register_2_q, register_3_q, register_4_q, register_5_q, register_6_q,
       register_7_q, register_8_q;

  Decoder_part #(.select(3), .disabled(0)) decoder_1 (
    .out0(decoder_1_out0), .out1(decoder_1_out1), .out2(decoder_1_out2), .out3(decoder_1_out3),
    .out4(decoder_1_out4), .out5(decoder_1_out5), .out6(decoder_1_out6), .out7(decoder_1_out7),
    .sel(WriteRegister), .en(WriteEnable));
  Register #(.width(16)) register_1 (.D(WriteData), .en(decoder_1_out0), .Q(register_1_q), .clk(Clock));  // open: clr
  Register #(.width(16)) register_2 (.D(WriteData), .en(decoder_1_out1), .Q(register_2_q), .clk(Clock));  // open: clr
  Register #(.width(16)) register_3 (.D(WriteData), .en(decoder_1_out2), .Q(register_3_q), .clk(Clock));  // open: clr
  Register #(.width(16)) register_4 (.D(WriteData), .en(decoder_1_out3), .Q(register_4_q), .clk(Clock));  // open: clr
  Register #(.width(16)) register_5 (.D(WriteData), .en(decoder_1_out4), .Q(register_5_q), .clk(Clock));  // open: clr
  Register #(.width(16)) register_6 (.D(WriteData), .en(decoder_1_out5), .Q(register_6_q), .clk(Clock));  // open: clr
  Register #(.width(16)) register_7 (.D(WriteData), .en(decoder_1_out6), .Q(register_7_q), .clk(Clock));  // open: clr
  Register #(.width(16)) register_8 (.D(WriteData), .en(decoder_1_out7), .Q(register_8_q), .clk(Clock));  // open: clr
  Multiplexer #(.select(3), .width(16), .enable("false")) multiplexer_1 (
    .in0(register_1_q), .in1(register_2_q), .in2(register_3_q), .in3(register_4_q), .in4(register_5_q),
    .in5(register_6_q), .in6(register_7_q), .in7(register_8_q), .out(ReadData1), .sel(ReadRegister1));
  Multiplexer #(.select(3), .width(16), .enable("false")) multiplexer_2 (
    .in0(register_1_q), .in1(register_2_q), .in2(register_3_q), .in3(register_4_q), .in4(register_5_q),
    .in5(register_6_q), .in6(register_7_q), .in7(register_8_q), .out(ReadData2), .sel(ReadRegister2));
endmodule

module ShifterDecoder (
  input  [3:0] Opcode,
  output ShiftSrc,
  output ShiftertoReg,
  output RegWrite
);

  and and_1 (RegWrite, ~Opcode[3], Opcode[2], ~Opcode[1]);  // AND_Gate

  assign ShiftertoReg = RegWrite;
  assign ShiftSrc = Opcode[0];
endmodule

module Arith_Log_Decoder (
  input  [3:0] Opcode,
  input  Subop,
  output [3:0] ALUOperation,
  output RegWrite,
  output ALUSrc
);

  wire and_2_out, and_3_out, and_5_out, and_6_out, not_1_out, not_2_out, not_3_out, not_4_out, not_5_out,
       not_6_out, not_7_out, not_8_out, not_9_out, not_10_out, not_11_out, not_12_out, not_13_out,
       not_14_out, not_15_out, not_16_out, not_17_out, not_18_out, not_19_out, not_20_out, not_21_out;

  not not_1 (not_1_out, Opcode[3]);
  not not_2 (not_2_out, Opcode[2]);
  not not_3 (not_3_out, Subop);
  not not_4 (not_4_out, Opcode[3]);
  not not_5 (not_5_out, Opcode[2]);
  not not_6 (not_6_out, Opcode[1]);
  not not_7 (not_7_out, Opcode[0]);
  not not_8 (not_8_out, Opcode[3]);
  not not_9 (not_9_out, Opcode[2]);
  not not_10 (not_10_out, Subop);
  not not_11 (not_11_out, Opcode[3]);
  not not_12 (not_12_out, Opcode[2]);
  not not_13 (not_13_out, Opcode[1]);
  not not_14 (not_14_out, Opcode[3]);
  not not_15 (not_15_out, Opcode[2]);
  not not_16 (not_16_out, Opcode[1]);
  not not_17 (not_17_out, Opcode[3]);
  not not_18 (not_18_out, Opcode[2]);
  not not_19 (not_19_out, Opcode[3]);
  not not_20 (not_20_out, Opcode[2]);
  not not_21 (not_21_out, Opcode[1]);
  and and_1 (ALUOperation[3], not_1_out, not_2_out, Opcode[1], Opcode[0], not_3_out);
  and and_2 (and_2_out, not_4_out, not_5_out, not_6_out, not_7_out, Subop);
  and and_3 (and_3_out, not_8_out, not_9_out, Opcode[1], Opcode[0], not_10_out);
  and and_4 (ALUOperation[1], not_11_out, not_12_out, not_13_out);
  and and_5 (and_5_out, not_14_out, not_15_out, not_16_out);
  and and_6 (and_6_out, not_17_out, not_18_out, Opcode[0]);
  and and_7 (ALUSrc, not_19_out, not_20_out, not_21_out, Opcode[0]);
  or or_1 (ALUOperation[2], and_2_out, and_3_out);
  or or_2 (RegWrite, and_5_out, and_6_out);

  assign ALUOperation[0] = 1'b0;
endmodule

module Arith_Log (
  input  Opcode3,
  input  Opcode2,
  input  Opcode1,
  input  Opcode0,
  input  Unsigned,
  input  Subop,
  output ALUOp3,
  output ALUOp2,
  output ALUOp1,
  output ALUOp0,
  output RegWrite,
  output ALUSrc
);

  wire and_2_out, and_3_out, and_5_out, and_6_out, not_1_out, not_2_out, not_3_out, not_4_out, not_5_out,
       not_6_out, not_7_out, not_8_out, not_9_out, not_10_out, not_11_out, not_12_out, not_13_out,
       not_14_out, not_15_out, not_16_out, not_17_out, not_18_out, not_19_out, not_20_out, not_21_out;

  not not_1 (not_1_out, Opcode3);
  not not_2 (not_2_out, Opcode2);
  not not_3 (not_3_out, Subop);
  not not_4 (not_4_out, Opcode3);
  not not_5 (not_5_out, Opcode2);
  not not_6 (not_6_out, Opcode1);
  not not_7 (not_7_out, Opcode0);
  not not_8 (not_8_out, Opcode3);
  not not_9 (not_9_out, Opcode2);
  not not_10 (not_10_out, Subop);
  not not_11 (not_11_out, Opcode3);
  not not_12 (not_12_out, Opcode2);
  not not_13 (not_13_out, Opcode1);
  not not_14 (not_14_out, Opcode3);
  not not_15 (not_15_out, Opcode2);
  not not_16 (not_16_out, Opcode1);
  not not_17 (not_17_out, Opcode3);
  not not_18 (not_18_out, Opcode2);
  not not_19 (not_19_out, Opcode3);
  not not_20 (not_20_out, Opcode2);
  not not_21 (not_21_out, Opcode1);
  and and_1 (ALUOp3, not_1_out, not_2_out, Opcode1, Opcode0, not_3_out);
  and and_2 (and_2_out, not_4_out, not_5_out, not_6_out, not_7_out, Subop);
  and and_3 (and_3_out, not_8_out, not_9_out, Opcode1, Opcode0, not_10_out);
  and and_4 (ALUOp1, not_11_out, not_12_out, not_13_out);
  and and_5 (and_5_out, not_14_out, not_15_out, not_16_out);
  and and_6 (and_6_out, not_17_out, not_18_out, Opcode0);
  and and_7 (ALUSrc, not_19_out, not_20_out, not_21_out, Opcode0);
  or or_1 (ALUOp2, and_2_out, and_3_out);
  or or_2 (RegWrite, and_5_out, and_6_out);

  assign ALUOp0 = 1'b0;
endmodule

module one_bit_ALU (
  input  Ainvert,
  input  Binvert,
  input  CarryIn,
  input  [1:0] Operation,
  input  a,
  input  b,
  input  Less,
  output Result,
  output Set,
  output CarryOut
);

  wire and_1_out, multiplexer_1_out, multiplexer_2_out, not_1_out, not_2_out, or_1_out;

  not not_1 (not_1_out, a);
  Multiplexer #(.enable("false")) multiplexer_1 (.in0(a), .in1(not_1_out), .out(multiplexer_1_out), .sel(Ainvert));
  not not_2 (not_2_out, b);
  Multiplexer #(.enable("false")) multiplexer_2 (.in0(b), .in1(not_2_out), .out(multiplexer_2_out), .sel(Binvert));
  and and_1 (and_1_out, multiplexer_1_out, multiplexer_2_out);
  or or_1 (or_1_out, multiplexer_1_out, multiplexer_2_out);
  Adder #(.width(1)) adder_1 (.a(multiplexer_1_out), .b(multiplexer_2_out), .out(Set), .cin(CarryIn), .cout(CarryOut));
  Multiplexer #(.select(2), .enable("false")) multiplexer_3 (
    .in0(and_1_out), .in1(or_1_out), .in2(Set), .in3(Less), .out(Result), .sel(Operation));
endmodule

module sixteen_bit_ALU (
  input  [3:0] ALUOperation,
  input  [15:0] a,
  input  [15:0] b,
  output [15:0] Result,
  output Zero,
  output Overflow
);

  wire one_bit_alu_1_carryout, one_bit_alu_2_carryout, one_bit_alu_3_carryout, one_bit_alu_4_carryout,
       one_bit_alu_5_carryout, one_bit_alu_6_carryout, one_bit_alu_7_carryout, one_bit_alu_8_carryout,
       one_bit_alu_9_carryout, one_bit_alu_10_carryout, one_bit_alu_11_carryout, one_bit_alu_12_carryout,
       one_bit_alu_13_carryout, one_bit_alu_14_carryout, one_bit_alu_15_carryout, one_bit_alu_16_carryout,
       one_bit_alu_16_set, xor_1_out;

  one_bit_ALU one_bit_alu_1 (
    .a(a[0]), .b(b[0]), .Less(xor_1_out), .Ainvert(ALUOperation[3]), .Binvert(ALUOperation[2]),
    .CarryIn(ALUOperation[2]), .Operation(ALUOperation[1:0]), .CarryOut(one_bit_alu_1_carryout),
    .Result(Result[0]));  // open: Set
  one_bit_ALU one_bit_alu_2 (
    .a(a[1]), .b(b[1]), .Less(1'b0), .Ainvert(ALUOperation[3]), .Binvert(ALUOperation[2]),
    .CarryIn(one_bit_alu_1_carryout), .Operation(ALUOperation[1:0]), .CarryOut(one_bit_alu_2_carryout),
    .Result(Result[1]));  // open: Set
  one_bit_ALU one_bit_alu_3 (
    .a(a[2]), .b(b[2]), .Less(1'b0), .Ainvert(ALUOperation[3]), .Binvert(ALUOperation[2]),
    .CarryIn(one_bit_alu_2_carryout), .Operation(ALUOperation[1:0]), .CarryOut(one_bit_alu_3_carryout),
    .Result(Result[2]));  // open: Set
  one_bit_ALU one_bit_alu_4 (
    .a(a[3]), .b(b[3]), .Less(1'b0), .Ainvert(ALUOperation[3]), .Binvert(ALUOperation[2]),
    .CarryIn(one_bit_alu_3_carryout), .Operation(ALUOperation[1:0]), .CarryOut(one_bit_alu_4_carryout),
    .Result(Result[3]));  // open: Set
  one_bit_ALU one_bit_alu_5 (
    .a(a[4]), .b(b[4]), .Less(1'b0), .Ainvert(ALUOperation[3]), .Binvert(ALUOperation[2]),
    .CarryIn(one_bit_alu_4_carryout), .Operation(ALUOperation[1:0]), .CarryOut(one_bit_alu_5_carryout),
    .Result(Result[4]));  // open: Set
  one_bit_ALU one_bit_alu_6 (
    .a(a[5]), .b(b[5]), .Less(1'b0), .Ainvert(ALUOperation[3]), .Binvert(ALUOperation[2]),
    .CarryIn(one_bit_alu_5_carryout), .Operation(ALUOperation[1:0]), .CarryOut(one_bit_alu_6_carryout),
    .Result(Result[5]));  // open: Set
  one_bit_ALU one_bit_alu_7 (
    .a(a[6]), .b(b[6]), .Less(1'b0), .Ainvert(ALUOperation[3]), .Binvert(ALUOperation[2]),
    .CarryIn(one_bit_alu_6_carryout), .Operation(ALUOperation[1:0]), .CarryOut(one_bit_alu_7_carryout),
    .Result(Result[6]));  // open: Set
  one_bit_ALU one_bit_alu_8 (
    .a(a[7]), .b(b[7]), .Less(1'b0), .Ainvert(ALUOperation[3]), .Binvert(ALUOperation[2]),
    .CarryIn(one_bit_alu_7_carryout), .Operation(ALUOperation[1:0]), .CarryOut(one_bit_alu_8_carryout),
    .Result(Result[7]));  // open: Set
  one_bit_ALU one_bit_alu_9 (
    .a(a[8]), .b(b[8]), .Less(1'b0), .Ainvert(ALUOperation[3]), .Binvert(ALUOperation[2]),
    .CarryIn(one_bit_alu_8_carryout), .Operation(ALUOperation[1:0]), .CarryOut(one_bit_alu_9_carryout),
    .Result(Result[8]));  // open: Set
  one_bit_ALU one_bit_alu_10 (
    .a(a[9]), .b(b[9]), .Less(1'b0), .Ainvert(ALUOperation[3]), .Binvert(ALUOperation[2]),
    .CarryIn(one_bit_alu_9_carryout), .Operation(ALUOperation[1:0]), .CarryOut(one_bit_alu_10_carryout),
    .Result(Result[9]));  // open: Set
  one_bit_ALU one_bit_alu_11 (
    .a(a[10]), .b(b[10]), .Less(1'b0), .Ainvert(ALUOperation[3]), .Binvert(ALUOperation[2]),
    .CarryIn(one_bit_alu_10_carryout), .Operation(ALUOperation[1:0]), .CarryOut(one_bit_alu_11_carryout),
    .Result(Result[10]));  // open: Set
  one_bit_ALU one_bit_alu_12 (
    .a(a[11]), .b(b[11]), .Less(1'b0), .Ainvert(ALUOperation[3]), .Binvert(ALUOperation[2]),
    .CarryIn(one_bit_alu_11_carryout), .Operation(ALUOperation[1:0]), .CarryOut(one_bit_alu_12_carryout),
    .Result(Result[11]));  // open: Set
  one_bit_ALU one_bit_alu_13 (
    .a(a[12]), .b(b[12]), .Less(1'b0), .Ainvert(ALUOperation[3]), .Binvert(ALUOperation[2]),
    .CarryIn(one_bit_alu_12_carryout), .Operation(ALUOperation[1:0]), .CarryOut(one_bit_alu_13_carryout),
    .Result(Result[12]));  // open: Set
  one_bit_ALU one_bit_alu_14 (
    .a(a[13]), .b(b[13]), .Less(1'b0), .Ainvert(ALUOperation[3]), .Binvert(ALUOperation[2]),
    .CarryIn(one_bit_alu_13_carryout), .Operation(ALUOperation[1:0]), .CarryOut(one_bit_alu_14_carryout),
    .Result(Result[13]));  // open: Set
  one_bit_ALU one_bit_alu_15 (
    .a(a[14]), .b(b[14]), .Less(1'b0), .Ainvert(ALUOperation[3]), .Binvert(ALUOperation[2]),
    .CarryIn(one_bit_alu_14_carryout), .Operation(ALUOperation[1:0]), .CarryOut(one_bit_alu_15_carryout),
    .Result(Result[14]));  // open: Set
  one_bit_ALU one_bit_alu_16 (
    .a(a[15]), .b(b[15]), .Less(1'b0), .Ainvert(ALUOperation[3]), .Binvert(ALUOperation[2]),
    .CarryIn(one_bit_alu_15_carryout), .Operation(ALUOperation[1:0]), .CarryOut(one_bit_alu_16_carryout),
    .Result(Result[15]), .Set(one_bit_alu_16_set));
  xor xor_1 (xor_1_out, one_bit_alu_16_set, Overflow);
  xor xor_2 (Overflow, one_bit_alu_15_carryout, one_bit_alu_16_carryout);
  nor nor_1 (Zero, Result[0], Result[1], Result[2], Result[3], Result[4], Result[5], Result[6], Result[7], Result[8], Result[9], Result[10], Result[11], Result[12], Result[13], Result[14], Result[15]);
endmodule

module PCDecoder (
  input  [3:0] Opcode,
  input  Subop,
  input  Zero,
  input  Less,
  output RegtoPC,
  output IMMtoPC,
  output ZerosToALU,
  output [3:0] ALUOp
);

  wire and_4_out, and_5_out, and_6_out, and_7_out, and_8_out, not_1_out, not_2_out, not_3_out, not_4_out,
       not_5_out, not_6_out, not_7_out, not_8_out, not_9_out, not_10_out, not_11_out, not_12_out, not_13_out,
       not_14_out, not_15_out, not_16_out;

  not not_1 (not_1_out, Opcode[2]);
  not not_2 (not_2_out, Opcode[1]);
  not not_3 (not_3_out, Subop);
  not not_4 (not_4_out, Opcode[2]);
  not not_5 (not_5_out, Opcode[1]);
  not not_6 (not_6_out, Opcode[0]);
  not not_7 (not_7_out, Opcode[2]);
  not not_8 (not_8_out, Opcode[1]);
  not not_9 (not_9_out, Zero);
  not not_10 (not_10_out, Opcode[2]);
  not not_11 (not_11_out, Zero);
  not not_12 (not_12_out, Opcode[0]);
  not not_13 (not_13_out, Zero);
  not not_14 (not_14_out, Less);
  not not_15 (not_15_out, Opcode[0]);
  and and_1 (ZerosToALU, Opcode[3], not_16_out);
  not not_16 (not_16_out, Opcode[2]);
  and and_2 (ALUOp[1], Opcode[3], not_1_out);
  and and_3 (RegtoPC, Opcode[3], Opcode[2], not_2_out, Opcode[0], not_3_out);
  and and_4 (and_4_out, Opcode[3], not_4_out, not_5_out, not_6_out, Zero);
  and and_5 (and_5_out, Opcode[3], not_7_out, not_8_out, Opcode[0], not_9_out);
  and and_6 (and_6_out, Opcode[3], not_10_out, Opcode[0], not_11_out, Less);
  and and_7 (and_7_out, Opcode[3], Opcode[1], not_12_out, not_13_out, not_14_out);
  and and_8 (and_8_out, Opcode[3], Opcode[2], Opcode[1], not_15_out);
  or or_1 (IMMtoPC, and_4_out, and_5_out, and_6_out, and_7_out, and_8_out);

  assign {ALUOp[3:2], ALUOp[0]} = 3'b000;
endmodule

module PCDecoderLogic (
  input  Opcode3,
  input  Opcode2,
  input  Opcode1,
  input  Opcode0,
  input  Subop,
  input  Zero,
  input  Less,
  output RegtoPC,
  output IMMtoPC,
  output OnestoALU
);

  wire and_2_out, and_3_out, and_4_out, and_5_out, and_6_out, not_1_out, not_2_out, not_3_out, not_4_out,
       not_5_out, not_6_out, not_7_out, not_8_out, not_9_out, not_10_out, not_11_out, not_12_out, not_13_out,
       not_14_out, not_15_out;

  not not_1 (not_1_out, Opcode1);
  not not_2 (not_2_out, Subop);
  not not_3 (not_3_out, Opcode2);
  not not_4 (not_4_out, Opcode1);
  not not_5 (not_5_out, Opcode0);
  not not_6 (not_6_out, Opcode2);
  not not_7 (not_7_out, Opcode1);
  not not_8 (not_8_out, Zero);
  not not_9 (not_9_out, Opcode2);
  not not_10 (not_10_out, Zero);
  not not_11 (not_11_out, Opcode0);
  not not_12 (not_12_out, Zero);
  not not_13 (not_13_out, Less);
  not not_14 (not_14_out, Opcode0);
  not not_15 (not_15_out, Opcode2);
  and and_1 (RegtoPC, Opcode3, Opcode2, not_1_out, Opcode0, not_2_out);
  and and_2 (and_2_out, Opcode3, not_3_out, not_4_out, not_5_out, Zero);
  and and_3 (and_3_out, Opcode3, not_6_out, not_7_out, Opcode0, not_8_out);
  and and_4 (and_4_out, Opcode3, not_9_out, Opcode0, not_10_out, Less);
  and and_5 (and_5_out, Opcode3, Opcode1, not_11_out, not_12_out, not_13_out);
  and and_6 (and_6_out, Opcode3, Opcode2, Opcode1, not_14_out);
  and and_7 (OnestoALU, Opcode3, not_15_out);
  or or_1 (IMMtoPC, and_2_out, and_3_out, and_4_out, and_5_out, and_6_out);
endmodule

module Decoder (
  input  [3:0] Opcode,
  input  Subop,
  input  Zero,
  input  Less,
  output ShiftSrc,
  output ShifterToReg,
  output RegWrite,
  output [3:0] ALUOp,
  output IMMtoALU,
  output RegtoPC,
  output IMMtoPC,
  output ZerosToALU,
  output MemWrite,
  output MemtoReg,
  output Halt,
  output LED,
  output WriteLED,
  output MemRead,
  output PCtoReg
);

  wire Arith_LogDecoder_regwrite, JALDecoder_immtopc, JALDecoder_regwrite, MemDecoder_regwrite,
       PCDecoder_immtopc, ShifterDecoder_regwrite;
  wire [3:0] Arith_LogDecoder_aluoperation, PCDecoder_aluop;

  ShifterDecoder ShifterDecoder (
    .Opcode(Opcode), .ShiftSrc(ShiftSrc), .ShiftertoReg(ShifterToReg), .RegWrite(ShifterDecoder_regwrite));
  Arith_Log_Decoder Arith_LogDecoder (
    .Opcode(Opcode), .Subop(Subop), .ALUOperation(Arith_LogDecoder_aluoperation),
    .RegWrite(Arith_LogDecoder_regwrite), .ALUSrc(IMMtoALU));
  PCDecoder PCDecoder (
    .Opcode(Opcode), .Subop(Subop), .Zero(Zero), .Less(Less), .RegtoPC(RegtoPC), .IMMtoPC(PCDecoder_immtopc),
    .ZerosToALU(ZerosToALU), .ALUOp(PCDecoder_aluop));
  MemDecoder MemDecoder (
    .Opcode(Opcode), .Subop(Subop), .MemWrite(MemWrite), .MemtoReg(MemtoReg), .RegWrite(MemDecoder_regwrite),
    .MemRead(MemRead));
  HaltDecoder haltdecoder_1 (.Opcode(Opcode), .Halt(Halt), .LED(LED));
  PutDecoder PutDecoder (.Opcode(Opcode), .WriteLED(WriteLED));
  JALDecoder JALDecoder (
    .Opcode(Opcode), .IMMtoPC(JALDecoder_immtopc), .PCtoReg(PCtoReg), .RegWrite(JALDecoder_regwrite));
  or or_1 (RegWrite, ShifterDecoder_regwrite, Arith_LogDecoder_regwrite, MemDecoder_regwrite, JALDecoder_regwrite);
  or or_2 (IMMtoPC, PCDecoder_immtopc, JALDecoder_immtopc);
  assign ALUOp = Arith_LogDecoder_aluoperation | PCDecoder_aluop;  // OR_Gate or_3, 4 bits wide
endmodule

module MemDecoder (
  input  [3:0] Opcode,
  input  Subop,
  output MemWrite,
  output MemtoReg,
  output RegWrite,
  output MemRead
);

  and and_1 (MemWrite, ~Opcode[0], Opcode[1], Opcode[2], ~Opcode[3], Subop);  // AND_Gate
  and and_2 (MemRead, ~Opcode[0], Opcode[1], Opcode[2], ~Opcode[3], ~Subop);  // AND_Gate

  assign MemtoReg = MemRead;
  assign RegWrite = MemRead;
endmodule

module HaltDecoder (
  input  [3:0] Opcode,
  output Halt,
  output LED
);

  and and_1 (Halt, ~Opcode[3], Opcode[2], Opcode[1], Opcode[0]);  // AND_Gate

  assign LED = Halt;
endmodule

module PutDecoder (
  input  [3:0] Opcode,
  output WriteLED
);

  and and_1 (WriteLED, Opcode[0], Opcode[1], Opcode[2], Opcode[3]);
endmodule

module JALDecoder (
  input  [3:0] Opcode,
  output IMMtoPC,
  output PCtoReg,
  output RegWrite
);

  and and_1 (IMMtoPC, ~Opcode[0], ~Opcode[1], Opcode[2], Opcode[3]);  // AND_Gate

  assign PCtoReg = IMMtoPC;
  assign RegWrite = IMMtoPC;
endmodule

module ResultToLess (
  input  [15:0] Result,
  output Less
);


  assign Less = Result[15];
endmodule

module ID_SECTION (
  input  [15:0] Instruction,
  input  Clock,
  input  [2:0] WriteReg,
  input  [15:0] WriteData,
  input  WriteEnable,
  input  [7:0] PC_PLUS1,
  output Subop,
  output [7:0] PC_PLUS1_2,
  output [15:0] ReadData1,
  output [15:0] ReadData2,
  output [15:0] IMM_ext
);

  wire Instruction_Splitter_unsigned;
  wire [2:0] Instruction_Splitter_readregister1, Instruction_Splitter_readregister2,
       Instruction_Splitter_writeregister;
  wire [3:0] Instruction_Splitter_opcode, Instruction_Splitter_shiftamount;
  wire [7:0] Instruction_Splitter_immediate;

  InstructionSplitter Instruction_Splitter (
    .Instruction(Instruction), .Opcode(Instruction_Splitter_opcode),
    .ReadRegister1(Instruction_Splitter_readregister1), .ReadRegister2(Instruction_Splitter_readregister2),
    .WriteRegister(Instruction_Splitter_writeregister), .ShiftAmount(Instruction_Splitter_shiftamount),
    .SubOp(Subop), .Unsigned(Instruction_Splitter_unsigned), .Immediate(Instruction_Splitter_immediate));
  Control control_1 ();
  RegisterFile Registers (
    .ReadRegister1(Instruction_Splitter_readregister1), .ReadRegister2(Instruction_Splitter_readregister2),
    .WriteRegister(WriteReg), .WriteData(WriteData), .WriteEnable(WriteEnable), .Clock(Clock),
    .ReadData1(ReadData1), .ReadData2(ReadData2));
  SignExtend Sign_Extend (
    .Unsigned(Instruction_Splitter_unsigned), .Immediate(Instruction_Splitter_immediate),
    .SignExtendedImm(IMM_ext));

  assign PC_PLUS1_2 = PC_PLUS1;

  // Notes on the sheet:
  //   Control
endmodule

module side (
  input  Op3,
  input  Op2,
  input  Op1,
  input  Op0,
  output Op3_2,
  output Op2_2,
  output Op1_2,
  output Op0_2
);

  wire not_1_out;

  and and_1 (Op1_2, Op3, not_1_out);
  not not_1 (not_1_out, Op2);

  assign Op0_2 = 1'b0;
  assign Op2_2 = 1'b0;
  assign Op3_2 = 1'b0;
endmodule

module IF_ID_LATCH (
  input  [15:0] Instruction_IN,
  input  [7:0] PC_PLUS1_IN,
  input  Clock,
  output [15:0] Instruction_OUT,
  output [7:0] PC_PLUS1_OUT
);

  Register #(.width(16)) register_1 (.D(Instruction_IN), .Q(Instruction_OUT), .clk(Clock));  // open: en, clr
  Register register_2 (.D(PC_PLUS1_IN), .Q(PC_PLUS1_OUT), .clk(Clock));  // open: en, clr
endmodule

module ID_EX_LATCH (
  input  in_1,
  input  in_2,
  input  in_3,
  input  in_4,
  input  in_5,
  input  in_6,
  input  in_7,
  input  in_8,
  input  in_9
);
endmodule

module IF_SECTION (
);

  wire button_1_out, not_1_out, undriven_2;
  wire [7:0] adder_1_out, PC_q, undriven;

  Register PC (.D(undriven), .en(not_1_out), .Q(PC_q), .clr(button_1_out));  // open: clk
  not not_1 (not_1_out, undriven_2);
  Button button_1 (.out(button_1_out));
  Adder adder_1 (.a(PC_q), .b(8'h1), .out(adder_1_out));  // open: cin, cout
  ROM #(.dataWidth(16)) rom_1 (.addr(PC_q), .sel(1'b1));  // open: data

  // Notes on the sheet:
  //   contents of rom_1 (hex, n*v repeats v):
  //   1 1104 241 1303 40 f000 241 1300 481 1503 281 6c1 1705 2c1 f200 901 1900 18ff f800 b41 1bf0 1b0f
  //   fa00 d81 1d19 fc1 1f20 3dc0 fc00 1 11e0 241 1378 3041 f000 481 150d 6c1 1708 44c0 f400 901 1910 b41
  //   1b04 4941 f800 d81 1d02 5c02 fc00 fc1 1f10 5e03 fe00 1 1140 61c1 63c0 f200 481 15ff 6c1 1701 845b
  //   865b 901 1900 985f b41 1b00 d81 1d00 1ce9 aa63 ac63 fc1 1f00 1 1119 be67 b067 e054 7000 c259 6c1
  //   170a f600 7000 d200 7000 fc1 1f01 fe00 7000 fc1 1f02 fe00 7000 fc1 1f03 fe00 7000 fc1 1f04 fe00 7000
endmodule

module EX_SECTION (
  input  [3:0] ALUOp,
  input  Subop,
  input  [15:0] ReadData1,
  input  EQZ_EQP,
  input  ShiftSrc,
  input  [3:0] Shamt,
  input  [15:0] ReadData2,
  input  [15:0] IMM_ext,
  input  IMMtoALU,
  input  ZeroestoALU,
  input  Branch,
  output Branch_2,
  output [15:0] ALU_OUT
);

  wire ALU_zero, multiplexer_3_out, not_1_out, resulttoless_1_less;
  wire [15:0] multiplexer_1_out, multiplexer_2_out;

  Shifter Shifter (
    .Subop(Subop), .Data(ReadData1), .ShamtReg(ReadData2), .ShiftSrc(ShiftSrc), .Shamt(Shamt));  // open: ShiftOut
  Multiplexer #(.width(16), .enable("false")) multiplexer_1 (
    .in0(ReadData2), .in1(IMM_ext), .out(multiplexer_1_out), .sel(IMMtoALU));
  Multiplexer #(.width(16), .enable("false")) multiplexer_2 (
    .in0(multiplexer_1_out), .in1({16{1'b0}}), .out(multiplexer_2_out), .sel(ZeroestoALU));
  ResultToLess resulttoless_1 (.Result(ALU_OUT), .Less(resulttoless_1_less));
  sixteen_bit_ALU ALU (
    .ALUOperation(ALUOp), .a(ReadData1), .b(multiplexer_2_out), .Result(ALU_OUT), .Zero(ALU_zero));  // open: Overflow
  not not_1 (not_1_out, resulttoless_1_less);
  Multiplexer #(.enable("false")) multiplexer_3 (
    .in0(not_1_out), .in1(ALU_zero), .out(multiplexer_3_out), .sel(EQZ_EQP));
  and and_1 (Branch_2, multiplexer_3_out, Branch);

  // Notes on the sheet:
  //   R2/IMM
endmodule

module MEM_SECTION (
  input  [15:0] ReadData2,
  input  [15:0] in_2,
  input  MemWrite,
  input  MemRead,
  input  Clock,
  output [15:0] Data_OUT
);

  wire [7:0] alutopc_1_address;

  ALUtoPC alutopc_1 (.ALUOut(ReadData2), .Address(alutopc_1_address));
  RAM #(.dataWidth(16), .bus("separate")) ram_1 (
    .addr(alutopc_1_address), .din(in_2), .data(Data_OUT), .str(MemWrite), .sel(1'b1), .clk(Clock),
    .ld(MemRead));  // open: clr
endmodule

module WB_SECTION (
  input  [15:0] Data_OUT,
  input  MemtoReg,
  input  [15:0] ALU_OUT,
  input  PCtoReg,
  input  ShifterToReg,
  input  [15:0] Shifter_OUT,
  input  [15:0] ReadData1,
  input  WriteLED,
  input  [15:0] PC_PLUS1,
  input  Clock,
  output [15:0] WriteData,
  output [15:0] LEDDIsplayOUT
);

  wire [15:0] multiplexer_1_out, multiplexer_2_out;

  Multiplexer #(.width(16), .enable("false")) multiplexer_1 (
    .in0(ALU_OUT), .in1(Data_OUT), .out(multiplexer_1_out), .sel(MemtoReg));
  Register #(.width(16)) register_1 (.D(ReadData1), .en(WriteLED), .Q(LEDDIsplayOUT), .clk(Clock));  // open: clr
  Multiplexer #(.width(16), .enable("false")) multiplexer_2 (
    .in0(multiplexer_1_out), .in1(Shifter_OUT), .out(multiplexer_2_out), .sel(ShifterToReg));
  Multiplexer #(.width(16), .enable("false")) multiplexer_3 (
    .in0(multiplexer_2_out), .in1(PC_PLUS1), .out(WriteData), .sel(PCtoReg));
endmodule

module MEM_WB_LATCH (
  input  [15:0] Data_OUT,
  input  [15:0] ALU_OUT,
  input  [15:0] ALU_OUT_2,
  input  [15:0] Shifter_OUT,
  input  [15:0] Shifter_OUT_2,
  input  [15:0] ReadData1,
  input  [15:0] ReadData1_2,
  input  [15:0] PC_PLUS1,
  input  [15:0] PC_PLUS1_2,
  input  [2:0] WriteRegister,
  input  [2:0] WriteRegister_2,
  input  [4:0] WB_CTRL,
  input  [4:0] WB_CTRL_2,
  input  Clock,
  output [15:0] Data_OUT_2
);

  Register #(.width(16)) register_1 (.D(Data_OUT), .clk(Clock));  // open: en, Q, clr
  Register #(.width(16)) register_2 (.D(ALU_OUT), .clk(Clock));  // open: en, Q, clr
  Register #(.width(16)) register_3 (.D(Shifter_OUT), .clk(Clock));  // open: en, Q, clr
  Register #(.width(16)) register_4 (.D(ReadData1), .clk(Clock));  // open: en, Q, clr
  Register #(.width(16)) register_5 (.D(PC_PLUS1), .clk(Clock));  // open: en, Q, clr
  Register #(.width(3)) register_6 (.D(WriteRegister), .clk(Clock));  // open: en, Q, clr
  Register #(.width(5)) register_7 (.D(WB_CTRL), .clk(Clock));  // open: en, Q, clr

  // Notes on the sheet:
  //   ShiftertoReg
  //   WB CONTROL
  //   MemtoReg
  //   PctoReg
  //   WriteLed
  //   WriteEnable
endmodule
